# Fritzing sketch Car_line (saved by Fritzing 0.9.3b)

parts:
  L298N2 = L298N DC motor driver
  M5 = DC Motor  # not connected
  M6 = DC Motor  # not connected
  M7 = DC Motor  # not connected
  M8 = DC Motor  # not connected
  Part1 = Arduino Nano (Rev3.0)
  VCC1 = Battery
  M9 = fc-51 [package=THT]
  M10 = fc-51 [package=THT]
  M11 = fc-51 [package=THT]
  M12 = fc-51 [package=THT]
  M13 = fc-51 [package=THT]

nets:
  GND: L298N2.GND, Part1.GND, VCC1.-, M9.pin2, M10.pin2, M11.pin2, M12.pin2, M13.pin2
  5V: L298N2.5V, Part1.VIN
  N1: L298N2.ENA, Part1.D3
  N2: L298N2.ENB, Part1.D6
  N3: L298N2.IN1, Part1.D4
  N4: L298N2.IN2, Part1.D8
  N5: L298N2.IN3, Part1.D5
  N6: L298N2.IN4, Part1.D7
  N7: Part1.5V, M9.pin3, M10.pin3, M11.pin3, M12.pin3, M13.pin3
  N8: Part1.A4, M9.pin1
  N9: Part1.A3, M10.pin1
  N10: Part1.A2, M13.pin1
  N11: Part1.A1, M12.pin1
  N12: Part1.A0, M11.pin1

custom parts:
  L298N DC motor driver: 2x DC motor driver with 78M05 positive voltage regulator (7..35 V) L298N: max 46 V, 2 A Set 5 V Enable jumper to enable 5 V regultor (needed for the L298N) and +5 V output at screw terminal or supply external +5 V at screw terminal Set ENA and/or ENB to +5 V to enable motor permanently or supply ENA and/or ENB with PWM signal IN1 and IN2 set rotation directory for motor A (OUT1/OUT2) IN2 and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
